# Fritzing sketch SuvaPlantH20v1 (saved by Fritzing 0.9.9b)
breadboards: 1

parts:
  Argon2 = Particle Argon
  Load_Cell1 = Load Cell - Red/white/black/green
  Part1 = HX711 Weighing Sensor Module

nets:
  3.3V: Argon2.3.3V, Part1.VCC
  GND: Argon2.GND, Part1.GND
  N1: Argon2.A2, Part1.DO/RX
  N2: Argon2.A5, Part1.CK/TX
  N3: Load_Cell1.wire1, Part1.E+
  N4: Load_Cell1.wire2, Part1.A-
  N5: Load_Cell1.wire3, Part1.E-
  N6: Load_Cell1.wire4, Part1.A+

custom parts:
  Particle Argon: The Argon is a powerful Wi-Fi enabled development board that can act as either a standalone Wi-Fi endpoint or Wi-Fi enabled gateway for Particle Mesh networks. It is based on the Nordic nRF52840 and has built-in battery charging circuitry so it’s easy to connect a Li-Po and deploy your local network in minutes. The Argon is great for connecting existing projects to the Particle Device Cloud or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
  Load Cell - Red/white/black/green: A rectangle load cell/weighting pressure Sensor with four wires - Red, white, black, green. Normally corresponding with E+, E-, A+, A- respectively.
