# Fritzing sketch SuvaPlantH20v2 (saved by Fritzing 0.9.9b)
breadboards: 3

parts:
  Breadboard4 = Breadboard Split Power
  Breadboard5 = Breadboard Split Power
  Argon1 = Particle Argon
  Part1 = 12 NeoPixel Ring [part_number=1643]
  Neopixel1 = Adafruit RBG Smart Neopixel [package="DIP (Dual Inline) [THT]"]
  Neopixel2 = Adafruit RBG Smart Neopixel [package="DIP (Dual Inline) [THT]"]
  Neopixel3 = Adafruit RBG Smart Neopixel [package="DIP (Dual Inline) [THT]"]
  Neopixel4 = Adafruit RBG Smart Neopixel [package="DIP (Dual Inline) [THT]"]
  WeMos_D1_Mini_OLED_Shield1 = WeMos D1 Mini OLED Shield  # not connected
  M1 = BMP280
  Grove1 = Grove Dust Sensor
  Capacitive_Soil_Moisture_Sensor1 = DFRobot Capacitive Soil Moisture Sensor V1.0 [part_number=SEN0193]
  WATER_PUMP1 = water pump/motor  # not connected
  Relay1 = Relay - 6 pins [package="DIP (Dual Inline) [THT]"]
  Q2 = TRANSISTOR_PNP [package=to-92]
  R2 = Resistor [tolerance=±5% resistance=2.2k package="0805 [SMD]"]
  R3 = Resistor [tolerance=±5% resistance=220 package="0805 [SMD]"]
  Part2 = MQ-131 breakout

nets:
  VCC: Breadboard4.pin3Y, Breadboard4.pin15Y, Breadboard4.pin17Y, Breadboard4.pin19Y, Breadboard4.pin29Y, Breadboard5.pin3Y, Breadboard5.pin15Y, Breadboard5.pin17Y, Breadboard5.pin29Y, Argon1.3.3V, M1.VIN, Grove1.VCC, Capacitive_Soil_Moisture_Sensor1.VCC, Relay1.VCC, Part2.VCC
  GND: Breadboard4.pin3Z, Breadboard4.pin20Z, Breadboard4.pin29Z, Breadboard5.pin3Z, Breadboard5.pin11Z, Breadboard5.pin29Z, Argon1.GND, Part1.GND, Neopixel1.+, Neopixel1.G, Neopixel2.+, Neopixel2.G, Neopixel3.+, Neopixel3.G, Neopixel4.+, Neopixel4.G, M1.GND, Grove1.GND, Capacitive_Soil_Moisture_Sensor1.GND, Relay1.GND, Q2.C, R2.Pin_1, Part2.GND
  N1: Argon1.A3, Part2.AO
  N2: Argon1.A5, Capacitive_Soil_Moisture_Sensor1.A
  N3: Argon1.MI, Q2.B, R2.Pin_0
  N4: Argon1.SDA, M1.SDA
  N5: Argon1.SCL, M1.SCL
  N6: Argon1.D4, Neopixel4.In
  N7: Argon1.D8, Grove1.SIG
  N8: Argon1.VUSB, Part1.VDD, Relay1.ON
  N9: Part1.IN, Neopixel1.O
  N10: Neopixel1.In, Neopixel2.O
  N11: Neopixel2.In, Neopixel3.O
  N12: Neopixel3.In, Neopixel4.O
  N13: Q2.E, R3.Pin_0

custom parts:
  Breadboard Split Power: A custom 6 pin per group power supply strip where the top row (ground) is all bussed together and the bottom row (+V) is split in two groups of 12 pins. This version is modified to be a loadable part and was rescaled to be on the standard 1px = 1thou grid with the size set in inches
  Particle Argon: The Argon is a powerful Wi-Fi enabled development board that can act as either a standalone Wi-Fi endpoint or Wi-Fi enabled gateway for Particle Mesh networks. It is based on the Nordic nRF52840 and has built-in battery charging circuitry so it’s easy to connect a Li-Po and deploy your local network in minutes. The Argon is great for connecting existing projects to the Particle Device Cloud or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
  12 NeoPixel Ring: 12 ultra bright smart LED NeoPixels are arranged in a circle with 1.5" (37mm) outer diameter. The rings are 'chainable' - connect the output pin of one to the input pin of another. Use only one microcontroller pin to control as many as you can chain together! Each LED is addressable as the driver chip is inside the LED. Each one has ~18mA constant current drive so the color will be very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
  BMP280: Temperature Humidity Barometric presure Sensor, I2C
  Grove Dust Sensor: PPD42 Grove Dust Sensor
  DFRobot Capacitive Soil Moisture Sensor V1.0: DFRobot Capacitive Soil Moisture Sensor V1.0 This product measures soil moisture levels by capacitive sensing, rather than resistive sensing like other types of moisture sensor. It is made of a corrosion resistant material giving it a long service life. Insert it into soil and impress your friends with the real-time soil moisture data! The product includes an on-board voltage regulator which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
  water pump/motor: WATER PUMP BY ARDUBLOCKTR
  Relay - 6 pins: A DIP stand-in part for whatever IC you want. With 6 pins on a 900mil dual inline package (DIP) footprint.
  MQ-131 breakout: SKU: 101282
